// Logisim project MyCPU.circ as structural Verilog: 11 circuits, main circuit main
module main (
  input  in_1,
  output [31:0] out_2,
  output out_3,
  output [4:0] out_4,
  output OverflowMain,
  output [31:0] out_6,
  output out_7,
  output [4:0] out_8,
  output [31:0] out_9
);

  wire alu_1_overflow, alu_1_zero, alucontorll_1_exceptionenable, ALUSrc, and_1_out, Branch, Branch2, clk,
       EXTOp, MemRead;
  wire [1:0] MemtoReg, RegDst;
  wire [2:0] alucontorll_1_out_4, controller_1_aluop;
  wire [31:0] adder_2_out, alu_1_result, dm_1_rd, ext_1_out, grf_1_rd1, multiplexer_2_out, multiplexer_3_out,
       multiplexer_4_out, pc4, PC_q, shift_1_out_3;

  // Probe on PC_q[6:2]
  IM im_1 (.A(PC_q[6:2]), .RD(out_2));
  // Probe on out_2
  // Probe on PC_q
  Controller controller_1 (
    .op(out_2[31:26]), .RegDst(RegDst), .ALUSrc(ALUSrc), .RegWrite(out_3), .MemRead(MemRead),
    .MemWrite(out_7), .MemtoReg(MemtoReg), .EXTOp(EXTOp), .Branch1(Branch), .Branch2(Branch2),
    .ALUOp(controller_1_aluop));
  Clock clock_1 (.out(clk));
  Register #(.width(32)) PC (.D(multiplexer_4_out), .Q(PC_q), .clk(clk), .clr(in_1));  // open: en
  Multiplexer #(.select(2), .width(5)) multiplexer_1 (
    .in0(out_2[20:16]), .in1(out_2[15:11]), .in2({5{1'b1}}), .out(out_4), .sel(RegDst));  // open: in3, en
  ALUContorll alucontorll_1 (
    .func(out_2[5:0]), .ALUop(controller_1_aluop), .ExceptionEnable(alucontorll_1_exceptionenable),
    .out_4(alucontorll_1_out_4));
  GRF grf_1 (
    .RA1(out_2[25:21]), .RA2(out_2[20:16]), .WA(out_4), .WD(out_6), .CLK(clk), .Reset(in_1),
    .RegWrite(out_3), .RD1(grf_1_rd1), .RD2(out_9));
  EXT ext_1 (.in(out_2[15:0]), .Extop(EXTOp), .out(ext_1_out));
  Adder #(.width(32)) adder_1 (.a(32'h4), .b(PC_q), .out(pc4));  // open: cin, cout
  Adder #(.width(32)) adder_2 (.a(pc4), .b(shift_1_out_3), .out(adder_2_out));  // open: cin, cout
  Shift shift_1 (.in_1(ext_1_out), .in_2(5'b00010), .out_3(shift_1_out_3));
  Multiplexer #(.width(32)) multiplexer_2 (
    .in0(out_9), .in1(ext_1_out), .out(multiplexer_2_out), .sel(ALUSrc));  // open: en
  Multiplexer #(.width(32)) multiplexer_3 (
    .in0(pc4), .in1(adder_2_out), .out(multiplexer_3_out), .sel(and_1_out));  // open: en
  and and_1 (and_1_out, alu_1_zero, Branch);
  ALU alu_1 (
    .A(grf_1_rd1), .B(multiplexer_2_out), .ALUCtrl(alucontorll_1_out_4), .Overflow(alu_1_overflow),
    .Result({alu_1_result[31:7], out_8, alu_1_result[1:0]}), .Zero(alu_1_zero));
  Multiplexer #(.width(32)) multiplexer_4 (
    .in0(multiplexer_3_out), .in1({multiplexer_3_out[31:28], out_2[25:0], 2'b00}), .out(multiplexer_4_out),
    .sel(Branch2));  // open: en
  and and_2 (OverflowMain, alu_1_overflow, alucontorll_1_exceptionenable);
  DM dm_1 (.A(out_8), .WD(out_9), .CLK(clk), .MemRead(MemRead), .MemWrite(out_7), .RD(dm_1_rd), .reset(in_1));
  Multiplexer #(.select(2), .width(32)) multiplexer_5 (
    .in0({alu_1_result[31:7], out_8, alu_1_result[1:0]}), .in1({out_2[15:0], {16{1'b0}}}), .in2(dm_1_rd),
    .in3(pc4), .out(out_6), .sel(MemtoReg));  // open: en

  // Other names for the same wires on the sheet: Instr[31:0] = out_2; j[27:2] = out_2[25:0]; MemAddr[4:0] = out_8;
  //   MemData[31:0] = out_9; MemWrite = out_7; RegAddr[4:0] = out_4; RegData[31:0] = out_6; RegWrite = out_3;
  //   Reset = in_1

  // Notes on the sheet:
  //   RS
  //   RT
  //   ALUOP
  //   func
  //   RA2
  //   imm16
  //   RA1
  //   WA
  //   WD
  //   ExceptionEnable
  //   RD1
  //   RD2
  //   ALUCtrl
  //   ALUCtrl
  //   A
  //   B
  //   Overflow
  //   Result
  //   Zero
  //   MemRead
  //   A
  //   WD
  //   MemWrite
  //   RD
endmodule

module IM (
  input  [4:0] A,
  output [31:0] RD
);

  ROM #(.addrWidth(5), .dataWidth(32)) rom_1 (.addr(A), .data(RD));  // open: sel

  // Notes on the sheet:
  //   contents of rom_1 (hex, n*v repeats v):
  //   340407cf 3485006f 3c063039 3c07ffff 34e7ffff 858021 e78821 f09021 928023 e78823 e49023 2519823
  //   34080000 ad040000 0 ad050004 ad100008 ad11000c ad120010 8d0f0000 8d0e0014 ad0e0018 8d0d000c 35080001
  //   35290001 354a0002 110affef 11090001 3c0b0457 10f4021
endmodule

module GRF (
  input  [4:0] RA1,
  input  CLK,
  input  Reset,
  input  RegWrite,
  input  [4:0] RA2,
  input  [4:0] WA,
  input  [31:0] WD,
  output [31:0] RD1,
  output [31:0] RD2
);

  wire [31:0] _0, _1, _2, _3, _4, _5, _6, _7, _8, _9, _10, _11, _12, _13, _14, _15, _16, _17, _18, _19, _20,
       _21, _22, _23, _24, _25, _26, _27, _28, _29, _30, _31, demultiplexer_1_out0, in1, in2, in3, in4, in5,
       in6, in7, in8, in9, in10, in11, in12, in13, in14, in15, in16, in17, in18, in19, in20, in21, in22,
       in23, in24, in25, in26, in27, in28, in29, in30, in31;

  Demultiplexer #(.select(5), .width(32), .tristate("true")) demultiplexer_1 (
    .out0(demultiplexer_1_out0), .out1(in1), .out2(in2), .out3(in3), .out4(in4), .out5(in5), .out6(in6),
    .out7(in7), .out8(in8), .out9(in9), .out10(in10), .out11(in11), .out12(in12), .out13(in13), .out14(in14),
    .out15(in15), .out16(in16), .out17(in17), .out18(in18), .out19(in19), .out20(in20), .out21(in21),
    .out22(in22), .out23(in23), .out24(in24), .out25(in25), .out26(in26), .out27(in27), .out28(in28),
    .out29(in29), .out30(in30), .out31(in31), .in(WD), .sel(WA));  // open: en
  Register #(.width(32)) register_1 (.D({32{1'b0}}), .en(RegWrite), .Q(_0), .clk(CLK), .clr(Reset));
  Register #(.width(32)) register_2 (.D(in4), .en(RegWrite), .Q(_4), .clk(CLK), .clr(Reset));
  Register #(.width(32)) register_3 (.D(in8), .en(RegWrite), .Q(_8), .clk(CLK), .clr(Reset));
  Register #(.width(32)) register_4 (.D(in12), .en(RegWrite), .Q(_12), .clk(CLK), .clr(Reset));
  Register #(.width(32)) register_5 (.D(in16), .en(RegWrite), .Q(_16), .clk(CLK), .clr(Reset));
  Register #(.width(32)) register_6 (.D(in20), .en(RegWrite), .Q(_20), .clk(CLK), .clr(Reset));
  Register #(.width(32)) register_7 (.D(in24), .en(RegWrite), .Q(_24), .clk(CLK), .clr(Reset));
  Register #(.width(32)) register_8 (.D(in28), .en(RegWrite), .Q(_28), .clk(CLK), .clr(Reset));
  Register #(.width(32)) register_9 (.D(in1), .en(RegWrite), .Q(_1), .clk(CLK), .clr(Reset));
  Register #(.width(32)) register_10 (.D(in5), .en(RegWrite), .Q(_5), .clk(CLK), .clr(Reset));
  Register #(.width(32)) register_11 (.D(in9), .en(RegWrite), .Q(_9), .clk(CLK), .clr(Reset));
  Register #(.width(32)) register_12 (.D(in13), .en(RegWrite), .Q(_13), .clk(CLK), .clr(Reset));
  Register #(.width(32)) register_13 (.D(in17), .en(RegWrite), .Q(_17), .clk(CLK), .clr(Reset));
  Register #(.width(32)) register_14 (.D(in21), .en(RegWrite), .Q(_21), .clk(CLK), .clr(Reset));
  Register #(.width(32)) register_15 (.D(in25), .en(RegWrite), .Q(_25), .clk(CLK), .clr(Reset));
  Register #(.width(32)) register_16 (.D(in29), .en(RegWrite), .Q(_29), .clk(CLK), .clr(Reset));
  Register #(.width(32)) register_17 (.D(in2), .en(RegWrite), .Q(_2), .clk(CLK), .clr(Reset));
  Register #(.width(32)) register_18 (.D(in6), .en(RegWrite), .Q(_6), .clk(CLK), .clr(Reset));
  Register #(.width(32)) register_19 (.D(in10), .en(RegWrite), .Q(_10), .clk(CLK), .clr(Reset));
  Register #(.width(32)) register_20 (.D(in14), .en(RegWrite), .Q(_14), .clk(CLK), .clr(Reset));
  Register #(.width(32)) register_21 (.D(in18), .en(RegWrite), .Q(_18), .clk(CLK), .clr(Reset));
  Register #(.width(32)) register_22 (.D(in22), .en(RegWrite), .Q(_22), .clk(CLK), .clr(Reset));
  Register #(.width(32)) register_23 (.D(in26), .en(RegWrite), .Q(_26), .clk(CLK), .clr(Reset));
  Register #(.width(32)) register_24 (.D(in30), .en(RegWrite), .Q(_30), .clk(CLK), .clr(Reset));
  Register #(.width(32)) register_25 (.D(in3), .en(RegWrite), .Q(_3), .clk(CLK), .clr(Reset));
  Register #(.width(32)) register_26 (.D(in7), .en(RegWrite), .Q(_7), .clk(CLK), .clr(Reset));
  Register #(.width(32)) register_27 (.D(in11), .en(RegWrite), .Q(_11), .clk(CLK), .clr(Reset));
  Register #(.width(32)) register_28 (.D(in15), .en(RegWrite), .Q(_15), .clk(CLK), .clr(Reset));
  Register #(.width(32)) register_29 (.D(in19), .en(RegWrite), .Q(_19), .clk(CLK), .clr(Reset));
  Register #(.width(32)) register_30 (.D(in23), .en(RegWrite), .Q(_23), .clk(CLK), .clr(Reset));
  Register #(.width(32)) register_31 (.D(in27), .en(RegWrite), .Q(_27), .clk(CLK), .clr(Reset));
  Register #(.width(32)) register_32 (.D(in31), .en(RegWrite), .Q(_31), .clk(CLK), .clr(Reset));
  Multiplexer #(.select(5), .width(32)) multiplexer_1 (
    .in0(_0), .in1(_1), .in2(_2), .in3(_3), .in4(_4), .in5(_5), .in6(_6), .in7(_7), .in8(_8), .in9(_9),
    .in10(_10), .in11(_11), .in12(_12), .in13(_13), .in14(_14), .in15(_15), .in16(_16), .in17(_17),
    .in18(_18), .in19(_19), .in20(_20), .in21(_21), .in22(_22), .in23(_23), .in24(_24), .in25(_25),
    .in26(_26), .in27(_27), .in28(_28), .in29(_29), .in30(_30), .in31(_31), .out(RD1), .sel(RA1));  // open: en
  Multiplexer #(.select(5), .width(32)) multiplexer_2 (
    .in0(_0), .in1(_1), .in2(_2), .in3(_3), .in4(_4), .in5(_5), .in6(_6), .in7(_7), .in8(_8), .in9(_9),
    .in10(_10), .in11(_11), .in12(_12), .in13(_13), .in14(_14), .in15(_15), .in16(_16), .in17(_17),
    .in18(_18), .in19(_19), .in20(_20), .in21(_21), .in22(_22), .in23(_23), .in24(_24), .in25(_25),
    .in26(_26), .in27(_27), .in28(_28), .in29(_29), .in30(_30), .in31(_31), .out(RD2), .sel(RA2));  // open: en

  // Other names for the same wires on the sheet: a1[4:0] = RA1; a2[4:0] = RA2; a3[4:0] = WA
endmodule

module Controller (
  input  [5:0] op,
  output [1:0] RegDst,
  output ALUSrc,
  output RegWrite,
  output MemRead,
  output MemWrite,
  output [1:0] MemtoReg,
  output EXTOp,
  output Branch1,
  output Branch2,
  output [2:0] ALUOp
);

  wire not_1_out, not_2_out, not_3_out, not_4_out, not_5_out, not_6_out;

  not not_1 (not_1_out, op[5]);
  not not_2 (not_2_out, op[3]);
  not not_3 (not_3_out, op[4]);
  not not_4 (not_4_out, op[1]);
  not not_5 (not_5_out, op[2]);
  not not_6 (not_6_out, op[0]);
  and R (RegDst[0], not_1_out, not_3_out, not_2_out, not_5_out, not_4_out, not_6_out);
  and lw (MemRead, op[5], not_3_out, not_2_out, not_5_out, op[1], op[0]);
  and sw (MemWrite, op[5], not_3_out, op[3], not_5_out, op[1], op[0]);
  and beq (Branch1, not_1_out, not_3_out, not_2_out, op[2], not_4_out, not_6_out);
  and lui (MemtoReg[0], not_1_out, not_3_out, op[3], op[2], op[1], op[0]);
  and ori (ALUOp[2], not_1_out, not_3_out, op[3], op[2], not_4_out, op[0]);
  and j (Branch2, not_1_out, not_3_out, not_2_out, not_5_out, op[1], op[0]);
  or or_1 (ALUSrc, MemRead, MemWrite, ALUOp[2]);
  or or_2 (RegWrite, RegDst[0], MemRead, MemtoReg[0], ALUOp[2]);
  or or_3 (ALUOp[1], Branch1, MemtoReg[0], ALUOp[2], Branch2);
  or or_4 (ALUOp[0], MemRead, MemWrite, Branch2, MemtoReg[0], ALUOp[2]);

  assign EXTOp = ALUOp[2];
  assign MemtoReg[1] = MemRead;
  assign RegDst[1] = Branch2;
endmodule

module ALU (
  input  [31:0] A,
  input  [31:0] B,
  input  [2:0] ALUCtrl,
  output Overflow,
  output [31:0] Result,
  output Zero
);

  wire and_2_out, and_3_out, and_4_out, and_5_out, not_1_out, not_2_out, not_3_out, not_4_out, not_5_out,
       not_6_out, or_2_out, or_3_out, or_4_out;
  wire [0:0] comparator_1_gt;
  wire [31:0] adder_1_out, and_1_out, or_1_out, subtractor_1_out;

  Adder #(.width(32)) adder_1 (.a(A), .b(B), .out(adder_1_out));  // open: cin, cout
  Subtractor #(.width(32)) subtractor_1 (.a(A), .b(B), .out(subtractor_1_out));  // open: bin, bout
  Comparator #(.width(32), .mode("unsigned")) comparator_1 (.a(A), .b(B), .gt(comparator_1_gt[0]));  // open: eq, lt
  assign and_1_out = A & B;  // AND_Gate and_1, 32 bits wide
  assign or_1_out = A | B;  // OR_Gate or_1, 32 bits wide
  or or_2 (or_2_out, and_2_out, and_3_out);
  and and_2 (and_2_out, A[31], B[31], not_2_out);
  not not_1 (not_1_out, A[31]);
  not not_2 (not_2_out, adder_1_out[31]);
  Multiplexer multiplexer_1 (.in0(or_2_out), .in1(or_3_out), .out(Overflow), .sel(ALUCtrl[0]));  // open: en
  and and_3 (and_3_out, not_1_out, not_3_out, adder_1_out[31]);
  not not_3 (not_3_out, B[31]);
  or or_3 (or_3_out, and_4_out, and_5_out);
  and and_4 (and_4_out, A[31], not_6_out, not_4_out);
  not not_4 (not_4_out, subtractor_1_out[31]);
  not not_5 (not_5_out, A[31]);
  not not_6 (not_6_out, B[31]);
  and and_5 (and_5_out, not_5_out, B[31], subtractor_1_out[31]);
  Multiplexer #(.select(3), .width(32)) multiplexer_2 (
    .in0(and_1_out), .in1(or_1_out), .in2(adder_1_out), .in3(subtractor_1_out),
    .in5({{31{1'b0}}, comparator_1_gt[0]}), .out(Result), .sel(ALUCtrl));  // open: in4, in6, in7, en
  or or_4 (or_4_out, subtractor_1_out[0], subtractor_1_out[1], subtractor_1_out[2], subtractor_1_out[3], subtractor_1_out[4], subtractor_1_out[5], subtractor_1_out[6], subtractor_1_out[7], subtractor_1_out[8], subtractor_1_out[9], subtractor_1_out[10], subtractor_1_out[11], subtractor_1_out[12], subtractor_1_out[13], subtractor_1_out[14], subtractor_1_out[15], subtractor_1_out[17], subtractor_1_out[18], subtractor_1_out[19], subtractor_1_out[20], subtractor_1_out[21], subtractor_1_out[22], subtractor_1_out[23], subtractor_1_out[24], subtractor_1_out[25], subtractor_1_out[26], subtractor_1_out[27], subtractor_1_out[28], subtractor_1_out[29], subtractor_1_out[30], subtractor_1_out[31], subtractor_1_out[16]);
  not not_7 (Zero, or_4_out);

  // Notes on the sheet:
  //   Add
  //   A_sign
  //   B_sign
  //   Add_sign
  //   Sub_sign
  //   Sub
endmodule

module DM (
  input  [4:0] A,
  input  [31:0] WD,
  input  CLK,
  input  reset,
  input  MemWrite,
  input  MemRead,
  output [31:0] RD
);

  RAM #(.addrWidth(5), .dataWidth(32), .bus("separate")) ram_1 (
    .addr(A), .din(WD), .data(RD), .str(MemWrite), .clk(CLK), .ld(MemRead), .clr(reset));  // open: sel
endmodule

module EXT (
  input  [15:0] in,
  input  Extop,
  output [31:0] out
);

  wire [31:0] bit_extender_1_out, bit_extender_2_out;

  assign bit_extender_1_out = {{16{in[15]}}, in};  // Bit_Extender bit_extender_1
  assign bit_extender_2_out = {{16{1'b0}}, in};  // Bit_Extender bit_extender_2
  Multiplexer #(.width(32)) multiplexer_1 (
    .in0(bit_extender_1_out), .in1(bit_extender_2_out), .out(out), .sel(Extop));  // open: en
endmodule

module IFU (
  input  zero,
  input  Branch,
  input  clk,
  input  reset,
  input  [31:0] imm32,
  output [31:0] Instr
);

  wire and_1_out;
  wire [4:0] PC_q_2;
  wire [31:0] adder_1_out, adder_2_out, multiplexer_1_out, PC_q, shift_1_out_3;

  IM im_1 (.A(PC_q_2), .RD(Instr));
  Register #(.width(32)) PC (
    .D(multiplexer_1_out), .Q({PC_q[31:7], PC_q_2, PC_q[1:0]}), .clk(clk), .clr(reset));  // open: en
  Adder #(.width(32)) adder_1 (.a(32'h4), .b({PC_q[31:7], PC_q_2, PC_q[1:0]}), .out(adder_1_out));  // open: cin, cout
  Adder #(.width(32)) adder_2 (.a(adder_1_out), .b(shift_1_out_3), .out(adder_2_out));  // open: cin, cout
  Shift shift_1 (.in_1(imm32), .in_2(5'b00010), .out_3(shift_1_out_3));
  Multiplexer #(.width(32)) multiplexer_1 (
    .in0(adder_1_out), .in1(adder_2_out), .out(multiplexer_1_out), .sel(and_1_out));  // open: en
  and and_1 (and_1_out, zero, Branch);

  // Notes on the sheet:
  //   Adder
  //   Nadd
  //        PCSrc
endmodule

module Shift (
  input  [31:0] in_1,
  input  [4:0] in_2,
  output [31:0] out_3
);

  Shifter #(.width(32)) shifter_1 (.in(in_1), .\dist (in_2), .out(out_3));
endmodule

// ALUControl
module ALUContorll (
  input  [5:0] func,
  input  [2:0] ALUop,
  output ExceptionEnable,
  output [2:0] out_4
);

  wire add_out, addu_out, beq_out, not_1_out, not_2_out, not_3_out, not_4_out, not_5_out, not_6_out,
       not_7_out, not_8_out, not_9_out, ori_out, sub_out, subu_out, sw_lw_out;

  not not_1 (not_1_out, ALUop[2]);
  not not_2 (not_2_out, ALUop[1]);
  not not_3 (not_3_out, ALUop[0]);
  not not_4 (not_4_out, func[5]);
  not not_5 (not_5_out, func[4]);
  not not_6 (not_6_out, func[2]);
  not not_7 (not_7_out, func[3]);
  not not_8 (not_8_out, func[1]);
  not not_9 (not_9_out, func[0]);
  and sw_lw (sw_lw_out, not_1_out, not_2_out, ALUop[0]);
  and beq (beq_out, not_1_out, ALUop[1], not_3_out);
  and lui___j (out_4[2], not_1_out, ALUop[1], ALUop[0]);
  and ori (ori_out, ALUop[2], ALUop[1], ALUop[0]);
  and addu (addu_out, not_1_out, not_2_out, not_3_out, func[5], not_5_out, not_7_out, not_6_out, not_8_out, func[0]);
  and subu (subu_out, not_1_out, not_2_out, not_3_out, func[5], not_5_out, not_7_out, not_6_out, func[1], func[0]);
  and add (add_out, not_1_out, not_2_out, not_3_out, func[5], not_5_out, not_7_out, not_6_out, not_8_out, not_9_out);
  and sub (sub_out, not_1_out, not_2_out, not_3_out, func[5], not_5_out, not_7_out, not_6_out, func[1], not_9_out);
  or or_1 (out_4[0], out_4[2], beq_out, ori_out, subu_out, sub_out);
  or or_2 (out_4[1], sub_out, out_4[2], sw_lw_out, subu_out, addu_out, beq_out, add_out);
  or or_3 (ExceptionEnable, sub_out, add_out);
endmodule

module j (
  input  Reset,
  output [31:0] out_2,
  output out_3,
  output [4:0] out_4,
  output [31:0] out_5,
  output out_6,
  output [4:0] out_7,
  output [31:0] out_8
);

  wire alu_1_zero, ALUSrc, and_1_out, Branch, Branch2, clk, EXTOp, MemRead;
  wire [1:0] MemtoReg, RegDst;
  wire [2:0] alucontorll_1_exceptionenable, controller_1_aluop;
  wire [3:0] multiplexer_3_out_2;
  wire [27:0] multiplexer_3_out;
  wire [31:0] adder_1_out, adder_2_out, alu_1_result, dm_1_rd, ext_1_out, grf_1_rd1, multiplexer_2_out,
       multiplexer_4_out, PC_q, shift_1_out_3;

  // Probe on PC_q[6:2]
  // Probe on out_2
  // Probe on PC_q
  IM im_1 (.A(PC_q[6:2]), .RD(out_2));
  Controller controller_1 (
    .op(out_2[31:26]), .RegDst(RegDst), .ALUSrc(ALUSrc), .RegWrite(out_3), .MemRead(MemRead),
    .MemWrite(out_6), .MemtoReg(MemtoReg), .EXTOp(EXTOp), .Branch1(Branch), .Branch2(Branch2),
    .ALUOp(controller_1_aluop));
  Clock clock_1 (.out(clk));
  Register #(.width(32)) PC (.D(multiplexer_4_out), .Q(PC_q), .clk(clk), .clr(Reset));  // open: en
  Multiplexer #(.width(5)) multiplexer_1 (
    .in0(out_2[20:16]), .in1(out_2[15:11]), .out(out_4), .sel(RegDst[0]));  // open: en
  ALUContorll alucontorll_1 (
    .func(out_2[5:0]), .ALUop(controller_1_aluop), .ExceptionEnable(alucontorll_1_exceptionenable[0]));  // open: out_4
  EXT ext_1 (.in(out_2[15:0]), .Extop(EXTOp), .out(ext_1_out));
  Adder #(.width(32)) adder_1 (.a(32'h4), .b(PC_q), .out(adder_1_out));  // open: cin, cout
  GRF grf_1 (
    .RA1(out_2[25:21]), .RA2(out_2[20:16]), .WA(out_4), .WD(out_5), .CLK(clk), .Reset(Reset),
    .RegWrite(out_3), .RD1(grf_1_rd1), .RD2(out_8));
  Shift shift_1 (.in_1(ext_1_out), .in_2(5'b00010), .out_3(shift_1_out_3));
  Multiplexer #(.width(32)) multiplexer_2 (
    .in0(out_8), .in1(ext_1_out), .out(multiplexer_2_out), .sel(ALUSrc));  // open: en
  Adder #(.width(32)) adder_2 (.a(adder_1_out), .b(shift_1_out_3), .out(adder_2_out));  // open: cin, cout
  ALU alu_1 (
    .A(grf_1_rd1), .B(multiplexer_2_out), .ALUCtrl(alucontorll_1_exceptionenable),
    .Result({alu_1_result[31:7], out_7, alu_1_result[1:0]}), .Zero(alu_1_zero));  // open: Overflow
  Multiplexer #(.width(32)) multiplexer_3 (
    .in0(adder_1_out), .in1(adder_2_out), .out({multiplexer_3_out_2, multiplexer_3_out}), .sel(and_1_out));  // open: en
  and and_1 (and_1_out, alu_1_zero, Branch);
  Multiplexer #(.width(32)) multiplexer_4 (
    .in0({multiplexer_3_out_2, multiplexer_3_out}), .in1({multiplexer_3_out_2, out_2[25:0], 2'b00}),
    .out(multiplexer_4_out), .sel(Branch2));  // open: en
  DM dm_1 (.A(out_7), .WD(out_8), .CLK(clk), .MemRead(MemRead), .MemWrite(out_6), .RD(dm_1_rd), .reset(Reset));
  Multiplexer #(.select(2), .width(32)) multiplexer_5 (
    .in0({alu_1_result[31:7], out_7, alu_1_result[1:0]}), .in1({out_2[15:0], {16{1'b0}}}), .in2(dm_1_rd),
    .out(out_5), .sel(MemtoReg));  // open: in3, en
  // Pins of 1 and 2 bits meet at RegDst
  // Pins of 1 and 3 bits meet at alucontorll_1_exceptionenable

  // Other names for the same wires on the sheet: Instr[31:0] = out_2; j[27:2] = out_2[25:0]; MemAddr[4:0] = out_7;
  //   MemData[31:0] = out_8; MemWrite = out_6; RegAddr[4:0] = out_4; RegData[31:0] = out_5; RegWrite = out_3

  // Notes on the sheet:
  //   OP
  //   func
  //   Rt
  //   Rd
  //   imm16
  //   Rs
  //   WD
  //   ALUCtrl
  //   Adder
  //   RD1
  //     RD2
  //   RegWrite
  //   Nadd
  //   ALUCtrl
  //   Zero
  //        PCSrc
  //   MemRead
  //   MemWrite
  //   A
  //   RD
  //   WD
endmodule
